// Logisim project CRC串行编码电路.circ as structural Verilog: 3 circuits, main circuit CRC(7,3)码编码电路
module \CRC_7_3_码编码电路  (
  input  \自动运算 
);

  wire clock_1_out, comparator_1_eq, d_ff_2_q, d_ff_3_q, multiplexer_1_out, not_1_out, Q0, Q1, Q2, Q3, Q4,
       shift_register_1_out, \复位控制_out ;
  wire [2:0] counter_1_q;

  Button \u_复位控制  (.out(\复位控制_out ));
  Clock clock_1 (.out(clock_1_out));
  Shift_Register #(.length(3)) shift_register_1 (
    .in(1'b0), .clk(clock_1_out), .out(shift_register_1_out), .clr(\复位控制_out ));  // open: shift, load, d0, q0, d1, q1, d2, q2
  Counter #(.width(3), .max('h7)) counter_1 (
    .count(multiplexer_1_out), .Q(counter_1_q), .clk(clock_1_out), .clr(\复位控制_out ));  // open: load, D, carry
  Comparator #(.width(3), .mode("unsigned")) comparator_1 (
    .a(counter_1_q), .b(3'b110), .eq(comparator_1_eq));  // open: gt, lt
  xor xor_1 (Q0, Q4, shift_register_1_out);
  Multiplexer #(.enable("false")) multiplexer_1 (.in0(1'b1), .in1(not_1_out), .out(multiplexer_1_out), .sel(\自动运算 ));
  not not_1 (not_1_out, comparator_1_eq);
  D_Flip_Flop d_ff_1 (
    .clk(clock_1_out), .D(Q0), .Q(Q1), .en(multiplexer_1_out), .reset(\复位控制_out ));  // open: Qn, preset
  D_Flip_Flop d_ff_2 (
    .clk(clock_1_out), .D(Q1), .Q(d_ff_2_q), .en(multiplexer_1_out), .reset(\复位控制_out ));  // open: Qn, preset
  xor xor_2 (Q2, Q4, d_ff_2_q);
  D_Flip_Flop d_ff_3 (
    .clk(clock_1_out), .D(Q2), .Q(d_ff_3_q), .en(multiplexer_1_out), .reset(\复位控制_out ));  // open: Qn, preset
  xor xor_3 (Q3, Q4, d_ff_3_q);
  Hex_Digit_Display hex_digit_display_1 (.value({3'b000, Q2}));  // open: dp
  Hex_Digit_Display hex_digit_display_2 (.value({3'b000, Q3}));  // open: dp
  // Probe on {Q3, Q2, Q1, Q0}
  D_Flip_Flop d_ff_4 (
    .clk(clock_1_out), .D(Q3), .Q(Q4), .en(multiplexer_1_out), .reset(\复位控制_out ));  // open: Qn, preset
  Hex_Digit_Display hex_digit_display_3 (.value({3'b000, Q1}));  // open: dp
  Hex_Digit_Display hex_digit_display_4 (.value({3'b000, Q0}));  // open: dp
  LED led_1 (.in(Q4));

  // Notes on the sheet:
  //   原始数据
  //   高位在右
  //   运算计数
  //   0
  //   x
  //   1*
  //   1
  //   x
  //   0*
  //   串行CRC编码电路（7,3）码
  //   生成多项式=11101
  //   2
  //   x
  //   1*
  //   3
  //   x
  //   1*
  //   CRC校验位
  //   4
  //   1*
  //   x
endmodule

module \CRC_7_4_码编码电路  (
  input  in_1,
  input  \自动运算 ,
  input  in_3,
  input  in_4,
  input  in_5,
  output out_6
);

  wire clock_1_out, comparator_1_eq, d_ff_1_q, multiplexer_1_out, not_1_out, Q0, Q1, Q2, Q3,
       shift_register_1_out, \复位控制_out ;
  wire [2:0] counter_1_q;

  Button \u_复位控制  (.out(\复位控制_out ));
  Clock clock_1 (.out(clock_1_out));
  Shift_Register #(.length(3)) shift_register_1 (
    .in(in_1), .clk(clock_1_out), .out(shift_register_1_out), .clr(\复位控制_out ));  // open: shift, load, d0, q0, d1, q1, d2, q2
  Counter #(.width(3), .max('h7)) counter_1 (
    .count(multiplexer_1_out), .Q(counter_1_q), .clk(clock_1_out), .clr(\复位控制_out ));  // open: load, D, carry
  Comparator #(.width(3), .mode("unsigned")) comparator_1 (
    .a(counter_1_q), .b(3'b110), .eq(comparator_1_eq));  // open: gt, lt
  xor xor_1 (Q0, Q3, shift_register_1_out);
  Multiplexer #(.enable("false")) multiplexer_1 (.in0(1'b1), .in1(not_1_out), .out(multiplexer_1_out), .sel(\自动运算 ));
  not not_1 (not_1_out, comparator_1_eq);
  Multiplexer multiplexer_2 (.in0(in_3), .in1(in_4), .out(out_6), .sel(in_5));  // open: en
  D_Flip_Flop d_ff_1 (
    .clk(clock_1_out), .D(Q0), .Q(d_ff_1_q), .en(multiplexer_1_out), .reset(\复位控制_out ));  // open: Qn, preset
  xor xor_2 (Q1, Q3, d_ff_1_q);
  D_Flip_Flop d_ff_2 (
    .clk(clock_1_out), .D(Q1), .Q(Q2), .en(multiplexer_1_out), .reset(\复位控制_out ));  // open: Qn, preset
  Hex_Digit_Display hex_digit_display_1 (.value({3'b000, Q2}));  // open: dp
  D_Flip_Flop d_ff_3 (
    .clk(clock_1_out), .D(Q2), .Q(Q3), .en(multiplexer_1_out), .reset(\复位控制_out ));  // open: Qn, preset
  Hex_Digit_Display hex_digit_display_2 (.value({3'b000, Q0}));  // open: dp
  Hex_Digit_Display hex_digit_display_3 (.value({3'b000, Q1}));  // open: dp
  LED led_1 (.in(Q3));

  // Notes on the sheet:
  //   原始数据
  //   高位在右
  //   运算计数
  //   0
  //   1*
  //   x
  //   1
  //   1*
  //   x
  //   生成多项式=1011
  //   串行CRC编码电路（7,4）码
  //   2
  //   0*
  //   x
  //   CRC校验位
  //   3
  //   1*
  //   x
endmodule

// Q0
module \CRC_22_16_码编码电路  (
  input  in_1,
  input  \自动运算 
);

  wire clock_1_out, comparator_1_eq, d_ff_2_q, multiplexer_1_out, not_1_out, Q0, Q1, Q2, Q3, Q4, Q5,
       shift_register_1_out, \复位控制_out ;
  wire [4:0] counter_1_q;

  Button \u_复位控制  (.out(\复位控制_out ));
  Clock clock_1 (.out(clock_1_out));
  Shift_Register #(.length(3)) shift_register_1 (
    .in(in_1), .clk(clock_1_out), .out(shift_register_1_out), .clr(\复位控制_out ));  // open: shift, load, d0, q0, d1, q1, d2, q2
  Counter #(.width(5), .max('h19)) counter_1 (
    .count(multiplexer_1_out), .Q(counter_1_q), .clk(clock_1_out), .clr(\复位控制_out ));  // open: load, D, carry
  Comparator #(.width(5), .mode("unsigned")) comparator_1 (
    .a(counter_1_q), .b(5'b10101), .eq(comparator_1_eq));  // open: gt, lt
  xor xor_1 (Q0, Q5, shift_register_1_out);
  Multiplexer #(.enable("false")) multiplexer_1 (.in0(1'b1), .in1(not_1_out), .out(multiplexer_1_out), .sel(\自动运算 ));
  not not_1 (not_1_out, comparator_1_eq);
  D_Flip_Flop d_ff_1 (
    .clk(clock_1_out), .D(Q0), .Q(Q1), .en(multiplexer_1_out), .reset(\复位控制_out ));  // open: Qn, preset
  D_Flip_Flop d_ff_2 (
    .clk(clock_1_out), .D(Q1), .Q(d_ff_2_q), .en(multiplexer_1_out), .reset(\复位控制_out ));  // open: Qn, preset
  xor xor_2 (Q2, Q5, d_ff_2_q);
  D_Flip_Flop d_ff_3 (
    .clk(clock_1_out), .D(Q2), .Q(Q3), .en(multiplexer_1_out), .reset(\复位控制_out ));  // open: Qn, preset
  D_Flip_Flop d_ff_4 (
    .clk(clock_1_out), .D(Q3), .Q(Q4), .en(multiplexer_1_out), .reset(\复位控制_out ));  // open: Qn, preset
  D_Flip_Flop d_ff_5 (
    .clk(clock_1_out), .D(Q4), .Q(Q5), .en(multiplexer_1_out), .reset(\复位控制_out ));  // open: Qn, preset
  LED led_1 (.in(Q5));
  Hex_Digit_Display hex_digit_display_1 (.value({3'b000, Q4}));  // open: dp
  Hex_Digit_Display hex_digit_display_2 (.value({3'b000, Q3}));  // open: dp
  Hex_Digit_Display hex_digit_display_3 (.value({3'b000, Q2}));  // open: dp
  Hex_Digit_Display hex_digit_display_4 (.value({3'b000, Q1}));  // open: dp
  Hex_Digit_Display hex_digit_display_5 (.value({3'b000, Q0}));  // open: dp

  // Notes on the sheet:
  //   原始数据
  //   高位在右
  //   运算计数
  //   0
  //   1*
  //   x
  //   1
  //   0*
  //   x
  //   串行CRC编码电路（22,16）码
  //   生成多项式=100101
  //   2
  //   x
  //   1*
  //   x
  //   0*
  //   3
  //   0*
  //   x
  //   4
  //   5
  //   x
  //   1*
  //   CRC校验位
endmodule
